# Fritzing sketch HC05_uno_commande_AT (saved by Fritzing 0.9.10b)

parts:
  Composant2 = Bluetooth HC-05 Macho
  R1 = Resistor [tolerance=±5% resistance=10k power=0.25 package=THT]
  R2 = Resistor [tolerance=±5% resistance=22k power=0.25 package=THT]
  Composant3 = Arduino Uno (Rev3)
  R3 = Resistor [tolerance=±5% resistance=10k power=0.25 package=THT]
  R4 = Resistor [tolerance=±5% resistance=22k power=0.25 package=THT]

nets:
  N1: Composant2.TXD, Composant3.D10_PWM/SS
  VCC: Composant2.VCC, Composant3.5V
  N2: Composant2.Key, R3.Pin_1, R4.Pin_0
  N3: R1.Pin_0, Composant3.D11_PWM/MOSI
  N4: R1.Pin_1, R2.Pin_0
  N5: R2.Pin_1, Composant3.GND, R4.Pin_1
  N6: Composant3.D5_PWM, R3.Pin_0

notes:
  Passage en commande AT logiciel
