# Fritzing sketch schema_SBP (saved by Fritzing 0.9.10b)

parts:
  DC_Mot_Enc1 = DC Motor with two-phase hall-encoder [part_number=VT-E-G25A-06-177E]
  S1 = H-Bridge with L298N
  Composant1 = Arduino Uno (Rev3)
  BAT1 = Battery Holders [package=lipo-1100mAh]
  Composant2 = ACS712 Low Current Sensor Board v12

nets:
  N1: DC_Mot_Enc1.pin1, Composant2.IP-
  N2: DC_Mot_Enc1.pin2, S1.M1-01
  5V: DC_Mot_Enc1.pin3, Composant1.5V, Composant2.5V
  GND: DC_Mot_Enc1.pin4, S1.GND, Composant1.GND, BAT1.-, Composant2.GND
  N3: DC_Mot_Enc1.pin5, Composant1.D3_PWM
  N4: DC_Mot_Enc1.pin6, Composant1.D5_PWM
  N5: S1.12V, BAT1.+
  N6: S1.ENA, S1.ENA-5V
  N7: S1.IN1, Composant1.D9_PWM
  N8: S1.IN2, Composant1.D10_PWM/SS
  N9: S1.ENB, S1.ENB-5V
  N10: S1.M1-02, Composant2.IP+
  N11: Composant1.A0, Composant2.VO

notes:
  Alimentation 7,4 V
  Respecter la couleur des fils sur le moteur réel (Rouge, Noir, Blanc Vert)
  Capteur de courant
  Pont en H
  Moto-reducteur + encodeur

custom parts:
  H-Bridge with L298N: h-bridge
