# Fritzing sketch BonnetConnectéEmetteurs (saved by Fritzing 0.9.10b)

parts:
  Composant2 = Bluetooth HC-05 Macho
  U2 = LIPO-110mAh [package=lipo-110]
  U3 = LIPO-110mAh [package=lipo-110]
  Composant5 = VERTER 5V USB Buck-Boost
  Composant6 = Bluetooth HC-05 Macho
  U4 = LIPO-110mAh [package=lipo-110]
  U5 = LIPO-110mAh [package=lipo-110]
  Composant7 = VERTER 5V USB Buck-Boost

nets:
  N1: Composant2.VCC, Composant5.5.0V
  GND: Composant2.GND, U3.-, Composant5.GND
  N2: U2.+, Composant5.VIN
  N3: U2.-, U3.+
  N4: Composant6.VCC, Composant7.5.0V
  GND_2: Composant6.GND, U5.-, Composant7.GND
  N5: U4.+, Composant7.VIN
  N6: U4.-, U5.+

notes:
  Bonnet connecté : Emetteurs

custom parts:
  VERTER 5V USB Buck-Boost: VERTER can take battery voltages from 3-12VDC and output a nice 5V DC, which makes it a perfect universal power supply for your portable project! Where Verter really shines is when you have a battery or power range that can fluctuate a lot, or you don't know what you'll end up using.
