# Fritzing sketch BonnetConnectéRécepteur (saved by Fritzing 0.9.10b)

parts:
  Composant2 = Bluetooth HC-05 Macho
  R1 = Resistor [tolerance=±5% resistance=10k power=0.25 package=THT]
  R2 = Resistor [tolerance=±5% resistance=22k power=0.25 package=THT]
  R3 = Resistor [tolerance=±5% resistance=10k power=0.25 package=THT]
  R4 = Resistor [tolerance=±5% resistance=22k power=0.25 package=THT]
  Composant4 = Arduino Nano (Rev3.0) (ICSP)
  U2 = LIPO-110mAh [package=lipo-110]
  U3 = LIPO-110mAh [package=lipo-110]
  U4 = Vibration Motor- ROB-08449 [package=vibe-motor-10mm]

nets:
  N1: Composant2.TXD, Composant4.D10
  VCC: Composant2.VCC, Composant4.5V
  N2: Composant2.Key, R3.Pin_1, R4.Pin_0
  N3: R1.Pin_0, Composant4.D11/MOSI
  N4: R1.Pin_1, R2.Pin_0
  N5: R2.Pin_1, R4.Pin_1, Composant4.GND, U3.-
  N6: R3.Pin_0, Composant4.D5
  N7: Composant4.D6, U4.-
  N8: Composant4.VIN, U2.+
  N9: U2.-, U3.+

notes:
  Bonnet connecté : Récepteur
  vibreur
